// Logisim project 6_11_24_lab9.circ as structural Verilog: 1 circuit, main circuit main
module main (
  input  in_1,
  input  in_2,
  input  s1,
  input  s0,
  input  Sleft,
  input  Sright,
  input  I3,
  input  I2,
  input  I0,
  input  I1,
  output out_11,
  output out_12,
  output out_13,
  output out_14
);

  wire clock_1_out, multiplexer_1_out, multiplexer_2_out, multiplexer_3_out, multiplexer_4_out;

  Clock clock_1 (.out(clock_1_out));
  D_Flip_Flop d_ff_1 (.D(multiplexer_1_out), .clk(clock_1_out), .Q(out_12), .preset(in_1), .reset(in_2));  // open: Qn
  Multiplexer #(.select(2)) multiplexer_1 (
    .in0(out_12), .in1(Sright), .in2(out_13), .in3(I3), .out(multiplexer_1_out), .sel({s1, s0}));
  D_Flip_Flop d_ff_2 (.D(multiplexer_2_out), .clk(clock_1_out), .Q(out_13), .preset(in_1), .reset(in_2));  // open: Qn
  Multiplexer #(.select(2)) multiplexer_2 (
    .in0(out_13), .in1(out_12), .in2(out_14), .in3(I2), .out(multiplexer_2_out), .sel({s1, s0}));
  D_Flip_Flop d_ff_3 (.D(multiplexer_3_out), .clk(clock_1_out), .Q(out_14), .preset(in_1), .reset(in_2));  // open: Qn
  Multiplexer #(.select(2)) multiplexer_3 (
    .in0(out_14), .in1(out_13), .in2(out_11), .in3(I1), .out(multiplexer_3_out), .sel({s1, s0}));
  D_Flip_Flop d_ff_4 (.D(multiplexer_4_out), .clk(clock_1_out), .Q(out_11), .preset(in_1), .reset(in_2));  // open: Qn
  Multiplexer #(.select(2)) multiplexer_4 (
    .in0(out_11), .in1(out_14), .in2(Sleft), .in3(I0), .out(multiplexer_4_out), .sel({s1, s0}));
endmodule
